# Fritzing sketch SmartCoil_sketch (saved by Fritzing 0.9.3b)

parts:
  proto1 = Adafruit_PermaProto_1_4_Board
  Raspberry_Pi_1 = Raspberry Pi 3 [part_number=RPI-3-V1.2]
  Part1 = Adafruit BME680  # not connected
  U1 = 4-Channel 5v Relay Shield [package=relay-4ch5v10a]
  U2 = Mystery Part - 5 pins [chip_label="Fan Coil Unit (wall)" package=THT]

nets:
  N1: proto1.connectorE6, Raspberry_Pi_1.GPIO17
  N2: proto1.connectorE7, Raspberry_Pi_1.GPIO27
  N3: proto1.connectorE8, Raspberry_Pi_1.GPIO22
  3V3: proto1.connectorW1, proto1.connectorZ1, Raspberry_Pi_1.3v3, Raspberry_Pi_1.3V3
  N4: proto1.connectorX1, Raspberry_Pi_1.GND
  N5: proto1.connectorY1, Raspberry_Pi_1.5V
  N6: proto1.connectorY14, U1.VCC
  N7: proto1.connectorZ8, U1.GND
  N8: U1.K1-Off, U1.K2-Off, U1.K3-Off, U1.K4-Off, U2.positive
  N9: U1.K1-On, U2.water_valve
  N10: U1.K2-On, U2.fan_lo_speed
  N11: U1.K3-On, U2.fan_mi_speed
  N12: U1.K4-On, U2.fan_hi_speed

notes:
  Fan Coil Unit (wall)
  water   fan low   fan mid   fan high
  valve    speed      speed      speed
  110V

custom parts:
  4-Channel 5v Relay Shield: 4 Channel 5v Relay Shield w. 2x SPD-06VDC-SD-C
  Mystery Part - 5 pins: A dummy, proxy, ersatz, stand-in part for whatever you want. With 5 pins on a 100 mil inline pin header footprint.
